# Fritzing sketch phoenicksboardv3 (saved by Fritzing 0.9.3b)
circuit board: 5.5cm x 5.7cm

parts:
  Raspberry_Pi_3 = Raspberry Pi 3 [part_number=RPI-3-V1.2]
  J1 = Power Jack [package=power_jack_pth]
  JP1 = Header 6 [package=molex-1x6-ra]
  J2 = AVR ISP 6 Pin [package=2x3-ns]
  J3 = AVR ISP 6 Pin [package=2x3-ns]

nets:
  N1: Raspberry_Pi_3.GPIO27, J3.6
  N2: Raspberry_Pi_3.GPIO22, J2.2
  N3: Raspberry_Pi_3.GPIO10, J3.3
  N4: Raspberry_Pi_3.GPIO9, J2.3
  N5: Raspberry_Pi_3.GPIO11, J2.1
  GND: Raspberry_Pi_3.GND, J1.GND, JP1.3, J2.4, J2.5, J3.1, J3.4
  N6: Raspberry_Pi_3.GPIO5, J3.5
  N7: Raspberry_Pi_3.GPIO6, JP1.6
  N8: Raspberry_Pi_3.GPIO13, JP1.5
  N9: Raspberry_Pi_3.GPIO19, JP1.2
  N10: Raspberry_Pi_3.GPIO26, JP1.1
  N11: Raspberry_Pi_3.5V, J2.6, J3.2
  N12: J1.PWR, JP1.4

notes:
  Dunce
  Golden
  Phoenicks™
  Version 3
  PWR
  GND
  M2
  M1
  L1
  L2
  LCD
  Raspberry Pi
